# Fritzing sketch Chema 1 - DHT, microSD, UNO or Wemos D1 (saved by Fritzing 0.9.4)
breadboards: 1

parts:
  microSD_Reader = MicroSD Card Module
  DHT11_/_DHT12_/_RHT1 = Humidity and Temperature Sensor RHT03
  Uno_/_Wemos_D1_WiFi = Arduino Uno (Rev3)

nets:
  GND: microSD_Reader.GND, DHT11_/_DHT12_/_RHT1.GND_2, Uno_/_Wemos_D1_WiFi.GND
  VCC: microSD_Reader.VCC, DHT11_/_DHT12_/_RHT1.Vcc, Uno_/_Wemos_D1_WiFi.5V
  N1: microSD_Reader.MISO, Uno_/_Wemos_D1_WiFi.D12/MISO
  N2: microSD_Reader.MOSI, Uno_/_Wemos_D1_WiFi.D11_PWM/MOSI
  N3: microSD_Reader.SCK, Uno_/_Wemos_D1_WiFi.D13/SCK
  N4: microSD_Reader.CS, Uno_/_Wemos_D1_WiFi.D10_PWM/SS
  N5: DHT11_/_DHT12_/_RHT1.Data-signal, Uno_/_Wemos_D1_WiFi.D2
